// Logisim project Basic Computer.circ as structural Verilog: 6 circuits, main circuit main
module main (
  input  Enable_Automated_Inputs,
  input  Memory_Write,
  input  Memory_Read,
  input  Manual_AR_Load,
  input  [2:0] Manual_Bus_SL,
  input  Manual_TR_Load,
  input  Manual_DR_Load,
  input  Manual_AC_Load,
  input  [2:0] Manual_ALU_SL,
  input  in_10,
  input  in_11,
  input  in_12,
  input  in_13
);

  wire AC_Load, and_1_out, AR_Load, clock_1_out, cu_1_hlt, digital_number_1_a, digital_number_1_b,
       digital_number_1_c, digital_number_1_d, digital_number_1_e, digital_number_1_f, digital_number_1_g,
       digital_number_2_a, digital_number_2_b, digital_number_2_c, digital_number_2_d, digital_number_2_e,
       digital_number_2_f, digital_number_2_g, digital_number_3_a, digital_number_3_b, digital_number_3_c,
       digital_number_3_d, digital_number_3_e, digital_number_3_f, digital_number_3_g, digital_number_4_a,
       digital_number_4_b, digital_number_4_c, digital_number_4_d, digital_number_4_e, digital_number_4_f,
       digital_number_4_g, digital_number_5_a, digital_number_5_b, digital_number_5_c, digital_number_5_d,
       digital_number_5_e, digital_number_5_f, digital_number_5_g, DR_Load, multiplexer_1_out,
       multiplexer_2_out, multiplexer_3_out, multiplexer_4_out, multiplexer_7_out, not_1_out, TR_Load;
  wire [2:0] ALU, Bus, multiplexer_5_out, multiplexer_8_out;
  wire [6:0] AR_q, bit_extender_1_out;
  wire [15:0] _16bits, AC_q, ALU_alu, bit_extender_2_out, DR_q, multiplexer_6_out, ram_1_data, TR_q;
  wire [19:0] Double_Dabble_output;

  CU cu_1 (
    .CLK(multiplexer_7_out), .TR_Load(TR_Load), .AC_Load(AC_Load), .AR_Load(AR_Load), .DR_Load(DR_Load),
    .Bus(Bus), .ALU(ALU), .HLT(cu_1_hlt), .Enable(Enable_Automated_Inputs));
  _16_Bits_Double_Dabble Double_Dabble (.Input(_16bits), .Output(Double_Dabble_output));
  _7_Segment_Display u_7_segment_display_1 (
    .g(digital_number_1_g), .f(digital_number_1_f), .a(digital_number_1_a), .b(digital_number_1_b),
    .e(digital_number_1_e), .d(digital_number_1_d), .c(digital_number_1_c));  // open: dp
  Digital_Number digital_number_1 (
    .A(digital_number_1_a), .B(digital_number_1_b), .C(digital_number_1_c), .D(digital_number_1_d),
    .E(digital_number_1_e), .F(digital_number_1_f), .G(digital_number_1_g),
    .Input(Double_Dabble_output[19:16]));
  Multiplexer multiplexer_1 (
    .in0(Manual_AR_Load), .in1(AR_Load), .out(multiplexer_1_out), .sel(Enable_Automated_Inputs));  // open: en
  Multiplexer multiplexer_2 (
    .in0(Manual_TR_Load), .in1(TR_Load), .out(multiplexer_2_out), .sel(Enable_Automated_Inputs));  // open: en
  Multiplexer multiplexer_3 (
    .in0(Manual_AC_Load), .in1(AC_Load), .out(multiplexer_3_out), .sel(Enable_Automated_Inputs));  // open: en
  _7_Segment_Display u_7_segment_display_2 (
    .g(digital_number_2_g), .f(digital_number_2_f), .a(digital_number_2_a), .b(digital_number_2_b),
    .e(digital_number_2_e), .d(digital_number_2_d), .c(digital_number_2_c));  // open: dp
  Digital_Number digital_number_2 (
    .A(digital_number_2_a), .B(digital_number_2_b), .C(digital_number_2_c), .D(digital_number_2_d),
    .E(digital_number_2_e), .F(digital_number_2_f), .G(digital_number_2_g),
    .Input(Double_Dabble_output[15:12]));
  Multiplexer multiplexer_4 (
    .in0(Manual_DR_Load), .in1(DR_Load), .out(multiplexer_4_out), .sel(Enable_Automated_Inputs));  // open: en
  _7_Segment_Display u_7_segment_display_3 (
    .g(digital_number_3_g), .f(digital_number_3_f), .a(digital_number_3_a), .b(digital_number_3_b),
    .e(digital_number_3_e), .d(digital_number_3_d), .c(digital_number_3_c));  // open: dp
  Bit_Extender #(.in_width(16), .out_width(7)) bit_extender_1 (.in(multiplexer_6_out), .out(bit_extender_1_out));
  ALU u_ALU (.ALU_SL(multiplexer_5_out), .DR(DR_q), .AC(AC_q), .ALU(ALU_alu));
  Digital_Number digital_number_3 (
    .A(digital_number_3_a), .B(digital_number_3_b), .C(digital_number_3_c), .D(digital_number_3_d),
    .E(digital_number_3_e), .F(digital_number_3_f), .G(digital_number_3_g), .Input(Double_Dabble_output[11:8]));
  Register #(.width(7)) AR (
    .D(bit_extender_1_out), .en(multiplexer_1_out), .Q(AR_q), .clk(multiplexer_7_out));  // open: clr
  Register #(.width(16)) TR (
    .D(multiplexer_6_out), .en(multiplexer_2_out), .Q(TR_q), .clk(multiplexer_7_out));  // open: clr
  Register #(.width(16)) DR (
    .D(multiplexer_6_out), .en(multiplexer_4_out), .Q(DR_q), .clk(multiplexer_7_out));  // open: clr
  Register #(.width(16)) AC (.D(ALU_alu), .en(multiplexer_3_out), .Q(AC_q), .clk(multiplexer_7_out));  // open: clr
  Multiplexer #(.width(3)) multiplexer_5 (
    .in0(Manual_ALU_SL), .in1(ALU), .out(multiplexer_5_out), .sel(Enable_Automated_Inputs));  // open: en
  _7_Segment_Display u_7_segment_display_4 (
    .g(digital_number_4_g), .f(digital_number_4_f), .a(digital_number_4_a), .b(digital_number_4_b),
    .e(digital_number_4_e), .d(digital_number_4_d), .c(digital_number_4_c));  // open: dp
  RAM #(.addrWidth(7), .dataWidth(16), .bus("separate")) ram_1 (
    .addr(AR_q), .din(multiplexer_6_out), .data(ram_1_data), .str(Memory_Write), .clk(multiplexer_7_out),
    .ld(Memory_Read));  // open: sel, clr
  assign bit_extender_2_out = {{9{1'b0}}, AR_q};  // Bit_Extender bit_extender_2
  Digital_Number digital_number_4 (
    .A(digital_number_4_a), .B(digital_number_4_b), .C(digital_number_4_c), .D(digital_number_4_d),
    .E(digital_number_4_e), .F(digital_number_4_f), .G(digital_number_4_g), .Input(Double_Dabble_output[7:4]));
  Multiplexer #(.select(3), .width(16), .enable("false")) multiplexer_6 (
    .in0(AC_q), .in1(DR_q), .in2(TR_q), .in3(bit_extender_2_out), .in4(ram_1_data), .out(multiplexer_6_out),
    .sel(multiplexer_8_out));  // open: in5, in6, in7
  Multiplexer multiplexer_7 (
    .in0(clock_1_out), .in1(and_1_out), .out(multiplexer_7_out), .sel(Enable_Automated_Inputs));  // open: en
  _7_Segment_Display u_7_segment_display_5 (
    .g(digital_number_5_g), .f(digital_number_5_f), .a(digital_number_5_a), .b(digital_number_5_b),
    .e(digital_number_5_e), .d(digital_number_5_d), .c(digital_number_5_c));  // open: dp
  Digital_Number digital_number_5 (
    .A(digital_number_5_a), .B(digital_number_5_b), .C(digital_number_5_c), .D(digital_number_5_d),
    .E(digital_number_5_e), .F(digital_number_5_f), .G(digital_number_5_g), .Input(Double_Dabble_output[3:0]));
  Multiplexer #(.width(3)) multiplexer_8 (
    .in0(Manual_Bus_SL), .in1(Bus), .out(multiplexer_8_out), .sel(Enable_Automated_Inputs));  // open: en
  and and_1 (and_1_out, clock_1_out, not_1_out);
  Clock clock_1 (.out(clock_1_out));
  not not_1 (not_1_out, cu_1_hlt);
  assign _16bits = in_13 ? bit_extender_2_out : 16'bz;  // Controlled_Buffer controlled_buffer_1
  assign _16bits = in_12 ? TR_q : 16'bz;  // Controlled_Buffer controlled_buffer_2
  assign _16bits = in_11 ? DR_q : 16'bz;  // Controlled_Buffer controlled_buffer_3
  assign _16bits = in_10 ? AC_q : 16'bz;  // Controlled_Buffer controlled_buffer_4

  // Other names for the same wires on the sheet: AC_Display = in_10; AR_Display = in_13; DR_Display = in_11;
  //   E = Enable_Automated_Inputs; TR_Display = in_12

  // Notes on the sheet:
  //   Step 2: Insert the Memory Inputs 
  //   Step 3: Simulate and enjoy
  //   Step 1: Enable Automated Inputs And Memory Read
endmodule

module ALU (
  input  [15:0] DR,
  input  [15:0] AC,
  input  [2:0] ALU_SL,
  output [15:0] ALU
);

  wire [15:0] adder_1_out, adder_2_out, and_1_out, multiplier_1_out, or_1_out, subtractor_1_out;

  Adder #(.width(16)) adder_1 (.a(DR), .b(AC), .out(adder_1_out));  // open: cin, cout
  Subtractor #(.width(16)) subtractor_1 (.a(DR), .b(AC), .out(subtractor_1_out));  // open: bin, bout
  Multiplier #(.width(16)) multiplier_1 (.a(DR), .b(AC), .out(multiplier_1_out));  // open: cin, cout
  Adder #(.width(16)) adder_2 (.a(DR), .b(16'h1), .out(adder_2_out));  // open: cin, cout
  assign or_1_out = DR | AC;  // OR_Gate or_1, 16 bits wide
  assign and_1_out = DR & AC;  // AND_Gate and_1, 16 bits wide
  Multiplexer #(.select(3), .width(16)) multiplexer_1 (
    .in1(DR), .in2(adder_1_out), .in3(subtractor_1_out), .in4(multiplier_1_out), .in5(adder_2_out),
    .in6(or_1_out), .in7(and_1_out), .out(ALU), .sel(ALU_SL));  // open: in0, en
endmodule

module CU (
  input  Enable,
  input  CLK,
  output HLT,
  output TR_Load,
  output AC_Load,
  output AR_Load,
  output DR_Load,
  output [2:0] Bus,
  output [2:0] ALU
);

  wire _1st, _2nd, _3rd, _4th, _5th, _6th_7th, _8th, _9th, _10th, _11th, _12th, _13th, _14th_15th, _16th;
  wire [3:0] counter_1_q;

  Counter #(.width(4), .max('hf)) counter_1 (.count(1'b1), .Q(counter_1_q), .clk(CLK));  // open: load, D, carry, clr
  Decoder #(.select(4)) decoder_1 (
    .out0(_1st), .out1(_2nd), .out2(_3rd), .out3(_4th), .out4(_5th), .out5(_6th_7th), .out6(_8th),
    .out7(_9th), .out8(_10th), .out9(_11th), .out10(_12th), .out11(_13th), .out12(_14th_15th), .out13(_16th),
    .out14(HLT), .sel(counter_1_q), .en(Enable));  // open: out15
  or or_1 (TR_Load, _1st, _9th);
  or or_2 (AC_Load, _3rd, _6th_7th, _8th, _11th, _14th_15th, _16th);
  or or_3 (AR_Load, _4th, _12th);
  or or_4 (DR_Load, _2nd, _5th, _6th_7th, _10th, _13th, _14th_15th);
  assign Bus = _2nd ? 3'b011 : 3'bz;  // Controlled_Buffer controlled_buffer_1
  assign ALU = _3rd ? 3'b101 : 3'bz;  // Controlled_Buffer controlled_buffer_2
  assign Bus = _4th ? 3'b000 : 3'bz;  // Controlled_Buffer controlled_buffer_3
  assign Bus = _5th ? 3'b100 : 3'bz;  // Controlled_Buffer controlled_buffer_4
  assign ALU = _6th_7th ? 3'b001 : 3'bz;  // Controlled_Buffer controlled_buffer_5
  assign Bus = _6th_7th ? 3'b010 : 3'bz;  // Controlled_Buffer controlled_buffer_6
  assign ALU = _8th ? 3'b100 : 3'bz;  // Controlled_Buffer controlled_buffer_7
  assign Bus = _1st ? 3'b100 : 3'bz;  // Controlled_Buffer controlled_buffer_8
  assign Bus = _9th ? 3'b000 : 3'bz;  // Controlled_Buffer controlled_buffer_9
  assign Bus = _10th ? 3'b011 : 3'bz;  // Controlled_Buffer controlled_buffer_10
  assign ALU = _11th ? 3'b101 : 3'bz;  // Controlled_Buffer controlled_buffer_11
  assign Bus = _12th ? 3'b000 : 3'bz;  // Controlled_Buffer controlled_buffer_12
  assign Bus = _13th ? 3'b100 : 3'bz;  // Controlled_Buffer controlled_buffer_13
  assign ALU = _14th_15th ? 3'b101 : 3'bz;  // Controlled_Buffer controlled_buffer_14
  assign Bus = _14th_15th ? 3'b010 : 3'bz;  // Controlled_Buffer controlled_buffer_15
  assign ALU = _16th ? 3'b011 : 3'bz;  // Controlled_Buffer controlled_buffer_16

  // Other names for the same wires on the sheet: ACL1 = _3rd; ACL3 = _8th; ACL4 = _11th; ACL6 = _16th; ARL1 = _4th;
  //   ARL2 = _12th; DRL1 = _2nd; DRL2 = _5th; ACL2 = _6th_7th; DRL3 = _6th_7th; DRL4 = _10th; DRL5 = _13th;
  //   ACL5 = _14th_15th; DRL6 = _14th_15th; TRL1 = _1st; TRL2 = _9th
endmodule

// Display
module Digital_Number (
  input  [3:0] Input,
  output A,
  output B,
  output C,
  output D,
  output E,
  output F,
  output G
);

  wire and_1_out, and_2_out, and_3_out, and_4_out, and_5_out, and_6_out, and_7_out, and_8_out, and_9_out,
       and_10_out, and_11_out, and_12_out, and_13_out, and_14_out, and_15_out, and_16_out, not_1_out,
       not_2_out, not_3_out, not_4_out, not_5_out, not_6_out, not_7_out, not_8_out, not_9_out, not_10_out,
       not_11_out, not_12_out, not_13_out, not_14_out, not_15_out, not_16_out, not_17_out, not_18_out,
       not_19_out, not_20_out, not_21_out;

  not not_1 (not_1_out, Input[2]);
  not not_2 (not_2_out, Input[0]);
  not not_3 (not_3_out, Input[1]);
  not not_4 (not_4_out, Input[0]);
  not not_5 (not_5_out, Input[1]);
  not not_6 (not_6_out, Input[2]);
  not not_7 (not_7_out, Input[0]);
  not not_8 (not_8_out, Input[2]);
  not not_9 (not_9_out, Input[0]);
  not not_10 (not_10_out, Input[1]);
  not not_11 (not_11_out, Input[2]);
  not not_12 (not_12_out, Input[0]);
  not not_13 (not_13_out, Input[0]);
  not not_14 (not_14_out, Input[1]);
  not not_15 (not_15_out, Input[0]);
  not not_16 (not_16_out, Input[1]);
  not not_17 (not_17_out, Input[0]);
  not not_18 (not_18_out, Input[2]);
  not not_19 (not_19_out, Input[1]);
  not not_20 (not_20_out, Input[0]);
  and and_1 (and_1_out, not_1_out, not_2_out);
  and and_2 (and_2_out, Input[2], Input[0]);
  not not_21 (not_21_out, Input[2]);
  and and_3 (and_3_out, not_3_out, not_4_out);
  and and_4 (and_4_out, Input[1], Input[0]);
  or or_1 (C, not_5_out, Input[0], Input[2], Input[3]);
  and and_5 (and_5_out, not_6_out, not_7_out);
  and and_6 (and_6_out, not_8_out, Input[1]);
  and and_7 (and_7_out, Input[1], not_9_out);
  and and_8 (and_8_out, Input[2], not_10_out, Input[0]);
  and and_9 (and_9_out, not_11_out, not_12_out);
  and and_10 (and_10_out, Input[1], not_13_out);
  and and_11 (and_11_out, not_14_out, not_15_out);
  and and_12 (and_12_out, Input[2], not_16_out);
  and and_13 (and_13_out, Input[2], not_17_out);
  and and_14 (and_14_out, not_18_out, Input[1]);
  and and_15 (and_15_out, Input[2], not_19_out);
  and and_16 (and_16_out, Input[2], not_20_out);
  or or_2 (A, and_1_out, Input[1], and_2_out, Input[3]);
  or or_3 (B, not_21_out, and_3_out, and_4_out);
  or or_4 (D, and_5_out, and_6_out, and_7_out, and_8_out, Input[3]);
  or or_5 (E, and_9_out, and_10_out);
  or or_6 (F, and_11_out, and_12_out, and_13_out, Input[3]);
  or or_7 (G, and_14_out, and_15_out, and_16_out, Input[3]);
endmodule

// Add3
module Add_3 (
  input  A3,
  input  A2,
  input  A1,
  input  A0,
  output B3,
  output B2,
  output B1,
  output B0
);

  wire and_1_out, and_2_out, and_3_out, and_4_out, and_5_out, and_6_out, and_7_out, and_8_out, and_9_out,
       and_10_out, and_11_out, and_12_out, not_1_out, not_2_out, not_3_out, not_4_out, not_5_out, not_6_out,
       not_7_out, not_8_out;

  and and_1 (and_1_out, A2, A0);
  and and_2 (and_2_out, A2, A1);
  and and_3 (and_3_out, A2, not_1_out, not_2_out);
  not not_1 (not_1_out, A1);
  not not_2 (not_2_out, A0);
  and and_4 (and_4_out, A3, A0);
  and and_5 (and_5_out, A3, A1);
  not not_3 (not_3_out, A2);
  and and_6 (and_6_out, not_3_out, A1);
  and and_7 (and_7_out, A1, A0);
  and and_8 (and_8_out, A3, not_4_out);
  not not_4 (not_4_out, A0);
  not not_5 (not_5_out, A3);
  not not_6 (not_6_out, A2);
  and and_9 (and_9_out, not_5_out, not_6_out, A0);
  and and_10 (and_10_out, A2, A1, not_7_out);
  not not_7 (not_7_out, A0);
  and and_11 (and_11_out, A3, not_8_out);
  not not_8 (not_8_out, A0);
  and and_12 (and_12_out, A3, A1);
  or or_1 (B3, and_1_out, and_2_out, A3);
  or or_2 (B2, and_3_out, and_4_out, and_5_out);
  or or_3 (B1, and_6_out, and_7_out, and_8_out);
  or or_4 (B0, and_9_out, and_10_out, and_11_out, and_12_out);
endmodule

module _16_Bits_Double_Dabble (
  input  [15:0] Input,
  output [19:0] Output
);

  wire add_3_1_b0, add_3_1_b1, add_3_1_b2, add_3_1_b3, add_3_2_b0, add_3_2_b1, add_3_2_b2, add_3_2_b3,
       add_3_3_b0, add_3_3_b1, add_3_3_b2, add_3_3_b3, add_3_4_b0, add_3_4_b1, add_3_4_b2, add_3_4_b3,
       add_3_5_b0, add_3_5_b1, add_3_5_b2, add_3_5_b3, add_3_6_b0, add_3_6_b1, add_3_6_b2, add_3_6_b3,
       add_3_7_b0, add_3_7_b1, add_3_7_b2, add_3_7_b3, add_3_8_b0, add_3_8_b1, add_3_8_b2, add_3_8_b3,
       add_3_9_b0, add_3_9_b1, add_3_9_b2, add_3_9_b3, add_3_10_b0, add_3_10_b1, add_3_10_b2, add_3_10_b3,
       add_3_11_b0, add_3_11_b1, add_3_11_b2, add_3_11_b3, add_3_12_b0, add_3_12_b1, add_3_12_b2,
       add_3_12_b3, add_3_13_b0, add_3_13_b1, add_3_13_b2, add_3_13_b3, add_3_14_b0, add_3_14_b1,
       add_3_14_b2, add_3_14_b3, add_3_15_b0, add_3_15_b1, add_3_15_b2, add_3_15_b3, add_3_16_b0,
       add_3_16_b1, add_3_16_b2, add_3_17_b0, add_3_17_b1, add_3_17_b2, add_3_17_b3, add_3_18_b0,
       add_3_18_b1, add_3_18_b2, add_3_18_b3, add_3_19_b0, add_3_19_b1, add_3_19_b2, add_3_19_b3,
       add_3_20_b0, add_3_20_b1, add_3_20_b2, add_3_20_b3, add_3_21_b0, add_3_21_b1, add_3_21_b2,
       add_3_21_b3, add_3_22_b0, add_3_22_b1, add_3_22_b2, add_3_22_b3, add_3_23_b0, add_3_23_b1,
       add_3_23_b2, add_3_24_b0, add_3_24_b1, add_3_24_b2, add_3_25_b0, add_3_25_b1, add_3_25_b2,
       add_3_25_b3, add_3_26_b0, add_3_26_b1, add_3_26_b2, add_3_26_b3, add_3_27_b0, add_3_27_b1,
       add_3_27_b2, add_3_27_b3, add_3_28_b0, add_3_28_b1, add_3_28_b2, add_3_28_b3, add_3_29_b0,
       add_3_29_b1, add_3_29_b2, add_3_29_b3, add_3_30_b0, add_3_30_b1, add_3_30_b2, add_3_30_b3;

  Add_3 add_3_1 (
    .A3(1'b0), .A2(Input[15]), .A1(Input[14]), .A0(Input[13]), .B3(add_3_1_b3), .B2(add_3_1_b2),
    .B1(add_3_1_b1), .B0(add_3_1_b0));
  Add_3 add_3_2 (
    .A3(add_3_1_b2), .A2(add_3_1_b1), .A1(add_3_1_b0), .A0(Input[12]), .B3(add_3_2_b3), .B2(add_3_2_b2),
    .B1(add_3_2_b1), .B0(add_3_2_b0));
  Add_3 add_3_3 (
    .A3(add_3_2_b2), .A2(add_3_2_b1), .A1(add_3_2_b0), .A0(Input[11]), .B3(add_3_3_b3), .B2(add_3_3_b2),
    .B1(add_3_3_b1), .B0(add_3_3_b0));
  Add_3 add_3_4 (
    .A3(1'b0), .A2(add_3_1_b3), .A1(add_3_2_b3), .A0(add_3_3_b3), .B3(add_3_4_b3), .B2(add_3_4_b2),
    .B1(add_3_4_b1), .B0(add_3_4_b0));
  Add_3 add_3_5 (
    .A3(add_3_3_b2), .A2(add_3_3_b1), .A1(add_3_3_b0), .A0(Input[10]), .B3(add_3_5_b3), .B2(add_3_5_b2),
    .B1(add_3_5_b1), .B0(add_3_5_b0));
  Add_3 add_3_6 (
    .A3(add_3_4_b2), .A2(add_3_4_b1), .A1(add_3_4_b0), .A0(add_3_5_b3), .B3(add_3_6_b3), .B2(add_3_6_b2),
    .B1(add_3_6_b1), .B0(add_3_6_b0));
  Add_3 add_3_7 (
    .A3(add_3_6_b2), .A2(add_3_6_b1), .A1(add_3_6_b0), .A0(add_3_8_b3), .B3(add_3_7_b3), .B2(add_3_7_b2),
    .B1(add_3_7_b1), .B0(add_3_7_b0));
  Add_3 add_3_8 (
    .A3(add_3_5_b2), .A2(add_3_5_b1), .A1(add_3_5_b0), .A0(Input[9]), .B3(add_3_8_b3), .B2(add_3_8_b2),
    .B1(add_3_8_b1), .B0(add_3_8_b0));
  Add_3 add_3_9 (
    .A3(add_3_8_b2), .A2(add_3_8_b1), .A1(add_3_8_b0), .A0(Input[8]), .B3(add_3_9_b3), .B2(add_3_9_b2),
    .B1(add_3_9_b1), .B0(add_3_9_b0));
  Add_3 add_3_10 (
    .A3(1'b0), .A2(add_3_4_b3), .A1(add_3_6_b3), .A0(add_3_7_b3), .B3(add_3_10_b3), .B2(add_3_10_b2),
    .B1(add_3_10_b1), .B0(add_3_10_b0));
  Add_3 add_3_11 (
    .A3(add_3_10_b2), .A2(add_3_10_b1), .A1(add_3_10_b0), .A0(add_3_12_b3), .B3(add_3_11_b3),
    .B2(add_3_11_b2), .B1(add_3_11_b1), .B0(add_3_11_b0));
  Add_3 add_3_12 (
    .A3(add_3_7_b2), .A2(add_3_7_b1), .A1(add_3_7_b0), .A0(add_3_9_b3), .B3(add_3_12_b3), .B2(add_3_12_b2),
    .B1(add_3_12_b1), .B0(add_3_12_b0));
  Add_3 add_3_13 (
    .A3(add_3_12_b2), .A2(add_3_12_b1), .A1(add_3_12_b0), .A0(add_3_14_b3), .B3(add_3_13_b3),
    .B2(add_3_13_b2), .B1(add_3_13_b1), .B0(add_3_13_b0));
  Add_3 add_3_14 (
    .A3(add_3_9_b2), .A2(add_3_9_b1), .A1(add_3_9_b0), .A0(Input[7]), .B3(add_3_14_b3), .B2(add_3_14_b2),
    .B1(add_3_14_b1), .B0(add_3_14_b0));
  Add_3 add_3_15 (
    .A3(add_3_14_b2), .A2(add_3_14_b1), .A1(add_3_14_b0), .A0(Input[6]), .B3(add_3_15_b3), .B2(add_3_15_b2),
    .B1(add_3_15_b1), .B0(add_3_15_b0));
  Add_3 add_3_16 (
    .A3(1'b0), .A2(add_3_10_b3), .A1(add_3_11_b3), .A0(add_3_17_b3), .B3(Output[19]), .B2(add_3_16_b2),
    .B1(add_3_16_b1), .B0(add_3_16_b0));
  Add_3 add_3_17 (
    .A3(add_3_11_b2), .A2(add_3_11_b1), .A1(add_3_11_b0), .A0(add_3_13_b3), .B3(add_3_17_b3),
    .B2(add_3_17_b2), .B1(add_3_17_b1), .B0(add_3_17_b0));
  Add_3 add_3_18 (
    .A3(add_3_17_b2), .A2(add_3_17_b1), .A1(add_3_17_b0), .A0(add_3_19_b3), .B3(add_3_18_b3),
    .B2(add_3_18_b2), .B1(add_3_18_b1), .B0(add_3_18_b0));
  Add_3 add_3_19 (
    .A3(add_3_13_b2), .A2(add_3_13_b1), .A1(add_3_13_b0), .A0(add_3_15_b3), .B3(add_3_19_b3),
    .B2(add_3_19_b2), .B1(add_3_19_b1), .B0(add_3_19_b0));
  Add_3 add_3_20 (
    .A3(add_3_19_b2), .A2(add_3_19_b1), .A1(add_3_19_b0), .A0(add_3_21_b3), .B3(add_3_20_b3),
    .B2(add_3_20_b2), .B1(add_3_20_b1), .B0(add_3_20_b0));
  Add_3 add_3_21 (
    .A3(add_3_15_b2), .A2(add_3_15_b1), .A1(add_3_15_b0), .A0(Input[5]), .B3(add_3_21_b3), .B2(add_3_21_b2),
    .B1(add_3_21_b1), .B0(add_3_21_b0));
  Add_3 add_3_22 (
    .A3(add_3_21_b2), .A2(add_3_21_b1), .A1(add_3_21_b0), .A0(Input[4]), .B3(add_3_22_b3), .B2(add_3_22_b2),
    .B1(add_3_22_b1), .B0(add_3_22_b0));
  Add_3 add_3_23 (
    .A3(add_3_16_b2), .A2(add_3_16_b1), .A1(add_3_16_b0), .A0(add_3_18_b3), .B3(Output[18]),
    .B2(add_3_23_b2), .B1(add_3_23_b1), .B0(add_3_23_b0));
  Add_3 add_3_24 (
    .A3(add_3_23_b2), .A2(add_3_23_b1), .A1(add_3_23_b0), .A0(add_3_25_b3), .B3(Output[17]),
    .B2(add_3_24_b2), .B1(add_3_24_b1), .B0(add_3_24_b0));
  Add_3 add_3_25 (
    .A3(add_3_18_b2), .A2(add_3_18_b1), .A1(add_3_18_b0), .A0(add_3_20_b3), .B3(add_3_25_b3),
    .B2(add_3_25_b2), .B1(add_3_25_b1), .B0(add_3_25_b0));
  Add_3 add_3_26 (
    .A3(add_3_25_b2), .A2(add_3_25_b1), .A1(add_3_25_b0), .A0(add_3_27_b3), .B3(add_3_26_b3),
    .B2(add_3_26_b2), .B1(add_3_26_b1), .B0(add_3_26_b0));
  Add_3 add_3_27 (
    .A3(add_3_20_b2), .A2(add_3_20_b1), .A1(add_3_20_b0), .A0(add_3_22_b3), .B3(add_3_27_b3),
    .B2(add_3_27_b2), .B1(add_3_27_b1), .B0(add_3_27_b0));
  Add_3 add_3_28 (
    .A3(add_3_27_b2), .A2(add_3_27_b1), .A1(add_3_27_b0), .A0(add_3_29_b3), .B3(add_3_28_b3),
    .B2(add_3_28_b2), .B1(add_3_28_b1), .B0(add_3_28_b0));
  Add_3 add_3_29 (
    .A3(add_3_22_b2), .A2(add_3_22_b1), .A1(add_3_22_b0), .A0(Input[3]), .B3(add_3_29_b3), .B2(add_3_29_b2),
    .B1(add_3_29_b1), .B0(add_3_29_b0));
  Add_3 add_3_30 (
    .A3(add_3_29_b2), .A2(add_3_29_b1), .A1(add_3_29_b0), .A0(Input[2]), .B3(add_3_30_b3), .B2(add_3_30_b2),
    .B1(add_3_30_b1), .B0(add_3_30_b0));
  Add_3 add_3_31 (
    .A3(add_3_24_b2), .A2(add_3_24_b1), .A1(add_3_24_b0), .A0(add_3_26_b3), .B3(Output[16]), .B2(Output[15]),
    .B1(Output[14]), .B0(Output[13]));
  Add_3 add_3_32 (
    .A3(add_3_26_b2), .A2(add_3_26_b1), .A1(add_3_26_b0), .A0(add_3_28_b3), .B3(Output[12]), .B2(Output[11]),
    .B1(Output[10]), .B0(Output[9]));
  Add_3 add_3_33 (
    .A3(add_3_28_b2), .A2(add_3_28_b1), .A1(add_3_28_b0), .A0(add_3_30_b3), .B3(Output[8]), .B2(Output[7]),
    .B1(Output[6]), .B0(Output[5]));
  Add_3 add_3_34 (
    .A3(add_3_30_b2), .A2(add_3_30_b1), .A1(add_3_30_b0), .A0(Input[1]), .B3(Output[4]), .B2(Output[3]),
    .B1(Output[2]), .B0(Output[1]));

  assign Output[0] = Input[0];
endmodule
